// Logisim project CPU.circ as structural Verilog: 3 circuits, main circuit RegisterBank
// REGS
module RegisterBank (
  input  [15:0] DATA_IN,
  input  CHIP_ENABLE,
  input  ZERO_ENABLE,
  input  [2:0] ADDR,
  input  READ_WRITE,
  output [15:0] DATA_OUT
);

  wire clock_1_out, decoder_1_out0, decoder_1_out1, decoder_1_out2, decoder_1_out3, decoder_1_out4,
       decoder_1_out5, decoder_1_out6, decoder_1_out7, not_1_out;
  wire [15:0] controlled_buffer_1_out, controlled_buffer_2_out, multiplexer_1_out, Reg0_q, Reg1_q, Reg2_q,
       Reg3_q, Reg4_q, Reg5_q, Reg6_q, Reg7_q;

  Pull_Resistor pull_resistor_1 (.node(READ_WRITE));
  Decoder #(.select(3), .disabled(0)) decoder_1 (
    .out0(decoder_1_out0), .out1(decoder_1_out1), .out2(decoder_1_out2), .out3(decoder_1_out3),
    .out4(decoder_1_out4), .out5(decoder_1_out5), .out6(decoder_1_out6), .out7(decoder_1_out7), .sel(ADDR),
    .en(READ_WRITE));
  Clock clock_1 (.out(clock_1_out));
  assign controlled_buffer_1_out = CHIP_ENABLE ? DATA_IN : 16'bz;  // Controlled_Buffer controlled_buffer_1
  not not_1 (not_1_out, READ_WRITE);
  assign controlled_buffer_2_out = READ_WRITE ? controlled_buffer_1_out : 16'bz;  // Controlled_Buffer controlled_buffer_2
  Register #(.width(16), .trigger("high")) Reg0 (
    .D(controlled_buffer_2_out), .en(decoder_1_out0), .Q(Reg0_q), .clk(clock_1_out), .clr(ZERO_ENABLE));
  Register #(.width(16), .trigger("high")) Reg1 (
    .D(controlled_buffer_2_out), .en(decoder_1_out1), .Q(Reg1_q), .clk(clock_1_out));  // open: clr
  Register #(.width(16), .trigger("high")) Reg2 (
    .D(controlled_buffer_2_out), .en(decoder_1_out2), .Q(Reg2_q), .clk(clock_1_out));  // open: clr
  Register #(.width(16), .trigger("high")) Reg3 (
    .D(controlled_buffer_2_out), .en(decoder_1_out3), .Q(Reg3_q), .clk(clock_1_out));  // open: clr
  Register #(.width(16), .trigger("high")) Reg4 (
    .D(controlled_buffer_2_out), .en(decoder_1_out4), .Q(Reg4_q), .clk(clock_1_out));  // open: clr
  Register #(.width(16), .trigger("high")) Reg5 (
    .D(controlled_buffer_2_out), .en(decoder_1_out5), .Q(Reg5_q), .clk(clock_1_out));  // open: clr
  Register #(.width(16), .trigger("high")) Reg6 (
    .D(controlled_buffer_2_out), .en(decoder_1_out6), .Q(Reg6_q), .clk(clock_1_out));  // open: clr
  Register #(.width(16), .trigger("high")) Reg7 (
    .D(controlled_buffer_2_out), .en(decoder_1_out7), .Q(Reg7_q), .clk(clock_1_out));  // open: clr
  Pull_Resistor pull_resistor_2 (.node(not_1_out));
  Multiplexer #(.select(3), .width(16)) multiplexer_1 (
    .in0(Reg0_q), .in1(Reg1_q), .in2(Reg2_q), .in3(Reg3_q), .in4(Reg4_q), .in5(Reg5_q), .in6(Reg6_q),
    .in7(Reg7_q), .out(multiplexer_1_out), .sel(ADDR), .en(not_1_out));
  assign DATA_OUT = CHIP_ENABLE ? multiplexer_1_out : 16'bz;  // Controlled_Buffer controlled_buffer_3

  // Notes on the sheet:
  //   DATA_IN: pull=down
  //   ADDR: pull=down
endmodule

module ALU (
  input  [2:0] OPCODE_IN,
  input  READ_WRITE,
  input  [15:0] DATA_IN,
  input  ADDR,
  input  CHIP_ENABLE,
  output [15:0] DATA_OUT,
  output REGA___REGB,
  output REGA___REGB_2,
  output REGA___REGB_3
);

  wire button_1_out, button_2_out, clock_1_out, decoder_1_out0, decoder_1_out1, not_1_out;
  wire [15:0] adder_1_out, controlled_buffer_1_out, controlled_buffer_2_out, multiplexer_1_out, nand_1_out,
       RegA_q, RegB_q;

  Button button_1 (.out(button_1_out));
  Decoder #(.disabled(0)) decoder_1 (.out0(decoder_1_out0), .out1(decoder_1_out1), .sel(ADDR), .en(READ_WRITE));
  Button button_2 (.out(button_2_out));
  assign controlled_buffer_1_out = CHIP_ENABLE ? DATA_IN : 16'bz;  // Controlled_Buffer controlled_buffer_1
  assign controlled_buffer_2_out = READ_WRITE ? controlled_buffer_1_out : 16'bz;  // Controlled_Buffer controlled_buffer_2
  Register #(.width(16), .trigger("high")) RegA (
    .D(controlled_buffer_2_out), .en(decoder_1_out0), .Q(RegA_q), .clk(clock_1_out), .clr(button_1_out));
  Clock clock_1 (.out(clock_1_out));
  Register #(.width(16), .trigger("high")) RegB (
    .D(controlled_buffer_2_out), .en(decoder_1_out1), .Q(RegB_q), .clk(clock_1_out), .clr(button_2_out));
  Adder #(.width(16)) adder_1 (.a(RegA_q), .b(RegB_q), .out(adder_1_out));  // open: cin, cout
  assign nand_1_out = ~(RegA_q & RegB_q);  // NAND_Gate nand_1, 16 bits wide
  Comparator #(.width(16)) comparator_1 (
    .a(RegA_q), .b(RegB_q), .gt(REGA___REGB), .eq(REGA___REGB_2), .lt(REGA___REGB_3));
  not not_1 (not_1_out, READ_WRITE);
  Multiplexer #(.select(3), .width(16)) multiplexer_1 (
    .in0(adder_1_out), .in1(adder_1_out), .in2(nand_1_out), .out(multiplexer_1_out), .sel(OPCODE_IN),
    .en(not_1_out));  // open: in3, in4, in5, in6, in7
  assign DATA_OUT = CHIP_ENABLE ? multiplexer_1_out : 16'bz;  // Controlled_Buffer controlled_buffer_3

  // Notes on the sheet:
  //   REGA___REGB: pull=down
  //   CHIP_ENABLE: pull=down
  //   REGA___REGB_3: pull=down
  //   DATA_IN: pull=down
  //   REGA___REGB_2: pull=down
endmodule

module CPU (
  input  DEBUG_ENABLE,
  input  in_2,
  input  [2:0] in_3,
  input  in_4,
  input  in_5,
  input  [15:0] in_6,
  input  in_7,
  input  in_8,
  input  in_9,
  input  in_10,
  input  [15:0] in_11,
  input  in_12,
  output BUS_R_W,
  output [15:0] out_14
);

  wire A_B, A_B_t, A_B_t_t, ALU_ENABLE, ALU_R_S, ALU_R_W, ALU_REG_SELECT, and_1_out, and_2_out, buffer_1_out,
       clock_1_out, clock_2_out, clock_3_out, ENA_R_0, ENA_R_1, ENA_R_A, ENA_R_B, ENA_R_C, IMM_ENABLE, NOP,
       not_1_out, not_2_out, not_3_out, not_4_out, not_5_out, not_6_out, not_7_out, or_1_out, or_2_out,
       or_3_out, or_4_out, PGC_INC, PGC_OVF, pull_resistor_1_node, REG_ENABLE, REG_R_W, RESET_M_PGM_CTR,
       SEL_RW_0, SEL_RW_1;
  wire [1:0] counter_2_q;
  wire [2:0] REG_ADDR;
  wire [6:0] IMM_7;
  wire [7:0] rom_2_data;
  wire [9:7] IMM_10;
  wire [15:0] bit_extender_1_out, bit_extender_2_out, controlled_buffer_6_out, DATA_BUS, rom_1_data;
  wire [15:10] INSTRUCTION;
  wire [22:0] counter_1_q, PGC_INP;

  RegisterBank RB1 (
    .DATA_IN(DATA_BUS), .DATA_OUT(DATA_BUS), .READ_WRITE(REG_R_W), .ADDR(REG_ADDR), .CHIP_ENABLE(REG_ENABLE),
    .ZERO_ENABLE(1'b1));
  assign REG_ADDR = ENA_R_A ? INSTRUCTION[12:10] : 3'bz;  // Controlled_Buffer controlled_buffer_1
  assign REG_ADDR = ENA_R_B ? IMM_10 : 3'bz;  // Controlled_Buffer controlled_buffer_2
  assign REG_ADDR = ENA_R_C ? IMM_7[2:0] : 3'bz;  // Controlled_Buffer controlled_buffer_3
  Counter #(.width(23), .max('h7fffff), .ongoal("load")) counter_1 (
    .D(PGC_INP), .count(PGC_INC), .Q(counter_1_q), .carry(PGC_OVF), .clk(clock_1_out));  // open: load, clr
  Clock clock_1 (.out(clock_1_out));
  // Probe on IMM_7
  // Probe on {IMM_10, IMM_7}
  ALU alu_1 (
    .DATA_IN(DATA_BUS), .DATA_OUT(DATA_BUS), .REGA___REGB(A_B), .REGA___REGB_2(A_B_t),
    .REGA___REGB_3(A_B_t_t), .ADDR(ALU_R_S), .READ_WRITE(ALU_R_W), .OPCODE_IN(INSTRUCTION[15:13]),
    .CHIP_ENABLE(ALU_ENABLE));
  assign DATA_BUS = not_1_out ? in_6 : 16'bz;  // Controlled_Buffer controlled_buffer_4
  not not_1 (not_1_out, BUS_R_W);
  // Probe on DATA_BUS
  assign out_14 = BUS_R_W ? DATA_BUS : 16'bz;  // Controlled_Buffer controlled_buffer_5
  assign controlled_buffer_6_out = DEBUG_ENABLE ? in_11 : 16'bz;  // Controlled_Buffer controlled_buffer_6
  // Probe on INSTRUCTION[15:13]
  // Probe on INSTRUCTION[12:10]
  // Probe on IMM_10
  // Probe on IMM_7[2:0]
  not not_2 (not_2_out, DEBUG_ENABLE);
  assign controlled_buffer_6_out = not_2_out ? rom_1_data : 16'bz;  // Controlled_Buffer controlled_buffer_7
  ROM #(.addrWidth(23), .dataWidth(16)) rom_1 (.addr(counter_1_q), .data(rom_1_data));  // open: sel
  Register #(.width(16), .trigger("high")) register_1 (
    .D(controlled_buffer_6_out), .en(in_12), .Q({INSTRUCTION, IMM_10, IMM_7}), .clk(clock_2_out));  // open: clr
  Clock clock_2 (.out(clock_2_out));
  or or_1 (or_1_out, ENA_R_0, ENA_R_1);
  Decoder #(.select(2), .disabled(0), .enable("false")) decoder_1 (
    .out1(ENA_R_A), .out2(ENA_R_B), .out3(ENA_R_C), .sel({ENA_R_1, ENA_R_0}));  // open: out0
  not not_3 (not_3_out, DEBUG_ENABLE);
  assign REG_ENABLE = not_3_out ? or_1_out : 1'bz;  // Controlled_Buffer controlled_buffer_8
  assign REG_R_W = DEBUG_ENABLE ? in_2 : 1'bz;  // Controlled_Buffer controlled_buffer_9
  assign REG_ADDR = DEBUG_ENABLE ? in_3 : 3'bz;  // Controlled_Buffer controlled_buffer_10
  assign ALU_REG_SELECT = DEBUG_ENABLE ? in_4 : 1'bz;  // Controlled_Buffer controlled_buffer_11
  assign ALU_R_W = DEBUG_ENABLE ? in_5 : 1'bz;  // Controlled_Buffer controlled_buffer_12
  assign BUS_R_W = DEBUG_ENABLE ? in_7 : 1'bz;  // Controlled_Buffer controlled_buffer_13
  assign RESET_M_PGM_CTR = DEBUG_ENABLE ? in_8 : 1'bz;  // Controlled_Buffer controlled_buffer_14
  assign REG_ENABLE = DEBUG_ENABLE ? in_9 : 1'bz;  // Controlled_Buffer controlled_buffer_15
  assign ALU_ENABLE = DEBUG_ENABLE ? in_10 : 1'bz;  // Controlled_Buffer controlled_buffer_16
  Counter #(.width(2), .max('h3), .trigger("falling")) counter_2 (
    .Q(counter_2_q), .clk(clock_3_out), .clr(or_2_out));  // open: load, D, count, carry
  Clock clock_3 (.out(clock_3_out));
  or or_2 (or_2_out, PGC_INC, NOP);
  Pull_Resistor #(.pull(1)) pull_resistor_1 (.node(pull_resistor_1_node));
  assign bit_extender_1_out = {{6{1'b0}}, {IMM_10, IMM_7}};  // Bit_Extender bit_extender_1
  ROM #(.addrWidth(5)) rom_2 (.addr({counter_2_q, INSTRUCTION[15:13]}), .data(rom_2_data), .sel(pull_resistor_1_node));
  not not_4 (not_4_out, INSTRUCTION[13]);
  not not_5 (not_5_out, INSTRUCTION[14]);
  buf buffer_1 (buffer_1_out, INSTRUCTION[15]);
  or or_3 (or_3_out, buffer_1_out, not_5_out, not_4_out);
  not not_6 (not_6_out, or_3_out);
  and and_1 (and_1_out, IMM_ENABLE, not_6_out);
  assign DATA_BUS = and_1_out ? bit_extender_1_out : 16'bz;  // Controlled_Buffer controlled_buffer_17
  nor nor_1 (NOP, IMM_7[0], IMM_7[1], IMM_7[2], IMM_7[3], IMM_7[4], IMM_7[5], IMM_7[6], IMM_10[7], IMM_10[8], IMM_10[9], INSTRUCTION[10], INSTRUCTION[11], INSTRUCTION[12], INSTRUCTION[13], INSTRUCTION[14], INSTRUCTION[15]);
  or or_4 (or_4_out, DEBUG_ENABLE, NOP);
  not not_7 (not_7_out, or_4_out);
  assign SEL_RW_0 = not_7_out ? rom_2_data[0] : 1'bz;  // Controlled_Buffer controlled_buffer_18
  Pull_Resistor pull_resistor_2 (.node(SEL_RW_0));
  Pull_Resistor pull_resistor_3 (.node(SEL_RW_1));
  assign SEL_RW_1 = not_7_out ? rom_2_data[1] : 1'bz;  // Controlled_Buffer controlled_buffer_19
  Pull_Resistor pull_resistor_4 (.node(ENA_R_0));
  assign ENA_R_0 = not_7_out ? rom_2_data[2] : 1'bz;  // Controlled_Buffer controlled_buffer_20
  assign ENA_R_1 = not_7_out ? rom_2_data[3] : 1'bz;  // Controlled_Buffer controlled_buffer_21
  assign ALU_R_S = not_7_out ? rom_2_data[4] : 1'bz;  // Controlled_Buffer controlled_buffer_22
  assign ALU_ENABLE = not_7_out ? rom_2_data[5] : 1'bz;  // Controlled_Buffer controlled_buffer_23
  assign IMM_ENABLE = not_7_out ? rom_2_data[6] : 1'bz;  // Controlled_Buffer controlled_buffer_24
  assign PGC_INC = not_7_out ? rom_2_data[7] : 1'bz;  // Controlled_Buffer controlled_buffer_25
  and and_2 (and_2_out, IMM_ENABLE, or_3_out);
  assign DATA_BUS = and_2_out ? bit_extender_2_out : 16'bz;  // Controlled_Buffer controlled_buffer_26
  assign bit_extender_2_out = {{9{1'b0}}, IMM_7};  // Bit_Extender bit_extender_2
  Pull_Resistor pull_resistor_5 (.node(ENA_R_1));
  Pull_Resistor pull_resistor_6 (.node(ALU_R_S));
  Pull_Resistor pull_resistor_7 (.node(ALU_ENABLE));
  Pull_Resistor pull_resistor_8 (.node(IMM_ENABLE));
  Pull_Resistor pull_resistor_9 (.node(PGC_INC));
  Decoder #(.select(2), .disabled(0), .enable("false")) decoder_2 (
    .out1(REG_R_W), .out2(ALU_R_W), .out3(BUS_R_W), .sel({2{SEL_RW_0}}));  // open: out0

  // Other names for the same wires on the sheet: OPCODE[2:0] = INSTRUCTION[15:13]; IMM_10[6:0] = IMM_7;
  //   INSTRUCTION[9:0] = {IMM_10, IMM_7}; RegC[2:0] = IMM_7[2:0]; RegB[2:0] = IMM_10; RegA[2:0] = INSTRUCTION[12:10]

  // Notes on the sheet:
  //   in_8: pull=down
  //   in_12: pull=down
  //   in_7: pull=down
  //   in_3: pull=down
  //   DEBUG_ENABLE: pull=down
  //   in_10: pull=down
  //   in_2: pull=down
  //   in_9: pull=down
  //   in_4: pull=down
  //   BUS_R_W: pull=down
  //   in_5: pull=down
  //   in_11: pull=down
  //   in_6: pull=down
  //   contents of rom_2 (hex, n*v repeats v):
  //   2a 3e 25 80 2a 70 25 80 2a 3e 25 80 45 80 0 0 7 80 0 0 5 80 0 0 26 80 0 0 5 8 80
endmodule
